# Fritzing sketch laermampel (saved by Fritzing 0.9.3b)
breadboards: 1

parts:
  Bauteil1 = Arduino Pro Mini v13
  U1 = NodeMCU V1.0
  C1 = Electrolytic Capacitor [capacitance=1mF voltage=20V package="100 mil [THT, electrolytic]"]
  Bauteil2 = Breakout Board for Electret Microphone
  C3 = Electrolytic Capacitor [capacitance=1mF voltage=20V package="100 mil [THT, electrolytic]"]
  NEOPIXEL1 = Neopixel Strip -- White (60/m)

nets:
  GND: Bauteil1.GND, U1.GND, C1.-, Bauteil2.GND, C3.-, NEOPIXEL1.GND
  VCC: Bauteil1.VCC, U1.Vin, C1.+, NEOPIXEL1.+5V
  N1: Bauteil1.A0, Bauteil2.VCC
  N2: Bauteil1.D10_PWM/SS, NEOPIXEL1.DI
  N3: Bauteil1.D1/RX, U1.TX
  N4: U1.3V3, Bauteil2.AUD, C3.+

custom parts:
  NodeMCU V1.0: ESP8266 based NodeMCU
  Neopixel Strip -- White (60/m): Neopixel Strip, White, 60 pixels per meter.
